// Digital circuit RF.dig as structural Verilog
module RF (
  input  [1:0] ReadRegister1,
  input  [1:0] ReadRegister2,
  input  [1:0] WriteReg,
  input  [3:0] WriteData,
  input  Clock,
  input  RegWrite,
  output [3:0] Read1,
  output [3:0] Read2
);

  wire and_1_out, and_2_out, and_3_out, and_4_out, decoder_1_out_0, decoder_1_out_1, decoder_1_out_2,
       decoder_1_out_3;
  wire [3:0] R0_q, R1_q, R2_q, R3_q;

  Decoder #(.Selector_Bits(2)) decoder_1 (
    .sel(WriteReg), .out_0(decoder_1_out_0), .out_1(decoder_1_out_1), .out_2(decoder_1_out_2),
    .out_3(decoder_1_out_3));
  and and_1 (and_1_out, decoder_1_out_0, RegWrite);
  and and_2 (and_2_out, decoder_1_out_1, RegWrite);
  and and_3 (and_3_out, decoder_1_out_2, RegWrite);
  and and_4 (and_4_out, decoder_1_out_3, RegWrite);
  Register #(.Bits(4)) R0 (.D(WriteData), .C(Clock), .en(and_1_out), .Q(R0_q));
  Register #(.Bits(4)) R1 (.D(WriteData), .C(Clock), .en(and_2_out), .Q(R1_q));
  Register #(.Bits(4)) R2 (.D(WriteData), .C(Clock), .en(and_3_out), .Q(R2_q));
  Register #(.Bits(4)) R3 (.D(WriteData), .C(Clock), .en(and_4_out), .Q(R3_q));
  Multiplexer #(.Selector_Bits(2), .Bits(4)) multiplexer_1 (
    .sel(ReadRegister1), .in_0(R0_q), .in_1(R1_q), .in_2(R2_q), .in_3(R3_q), .out(Read1));
  Multiplexer #(.Selector_Bits(2), .Bits(4)) multiplexer_2 (
    .sel(ReadRegister2), .in_0(R0_q), .in_1(R1_q), .in_2(R2_q), .in_3(R3_q), .out(Read2));
endmodule
